# Fritzing sketch rpi-arduino-i2c-reference (saved by Fritzing 0.9.3b)

parts:
  Part1 = Arduino Uno (Rev3) - ICSP
  Raspberry_Pi1 = Raspberry Pi B+

nets:
  N1: Part1.ICSP_MISO, Part1.D12/MISO, Part1.RESET
  GND: Part1.GND, Raspberry_Pi1.GND
  N2: Part1.A4/SDA, Raspberry_Pi1.GPIO2
  N3: Part1.A5/SCL, Raspberry_Pi1.GPIO3
